# Fritzing sketch smartfarm (saved by Fritzing 0.8.7b)
breadboards: 1

parts:
  U1 = Module 4 Relais 5V [package="Module 4 Relais 5V"]
  PS1 = prefix0000 [part_number=S-350-60]  # not connected
  U2 = ESP32-38PinWide [part_number=ESP32-38PinWide]
  YF-S201_Flow_Meter2 = YF-S201 Water Flow Meter
  U3 = WS2812 RGB LED strip

nets:
  GND: U1.GND, U2.GND, YF-S201_Flow_Meter2.GND, U3.GND
  N1: U1.IN1, U2.GPIO25
  N2: U1.IN2, U2.GPIO26
  N3: U1.K1-NF, U2.GPIO6
  N4: U1.K1-NO, YF-S201_Flow_Meter2.VCC
  N5: U1.K2-NO, U3.VCC

notes:
  dcdc converter
  12v plus
  12minus
  5v plus
  5v minus
  3v plus
  3v minus
  220+
  220-
  220접지
  power adapter
  +
  -

custom parts:
  Module 4 Relais 5V: Module 4 Relais 5V 4x SPD-06VDC-SD-C
  ESP32-38PinWide: Generic 38-Pin ESP32 with wide format (only access to one side of pins on a breadboard) based on Stephen Lilley's HiLetgo ESP-WROOM-32 ESP32 ESP-32S Development Board.
  YF-S201 Water Flow Meter: The YF-S201 Flow Meter. The input voltage is 5V to 24V (DC).
  WS2812 RGB LED strip: WS2812 strip
